# Fritzing sketch Circuit (saved by Fritzing 0.9.3b)
breadboards: 1

parts:
  Bauteil1 = Arduino Mega 2560 (Rev3)
  DHT11 = Humidity and Temperature Sensor DHT11
  Bauteil2 = HX711 Weighing Sensor Module  # not connected
  Sparkfun_HX711 = Sparkfun load cell amplifier
  M2 = fc-51 [package=THT]
  M3 = fc-51 [package=THT]
  Adafruit_DS3231_RTC = ZS-042 RTC Module
  A1 = Arduino GIGA R1 WiFi
  J1 = Basic Servo
  WL-134 = RFID RC522 SIP - 8 pins [chip_label="RFID RC522" package="SIP (Single Inline) [THT]"]

nets:
  N1: Bauteil1.D17_PWM/RX2, A1.Pin_129
  N2: Bauteil1.D16_PWM/TX2, A1.Pin_127, A1.Pin_128
  VCC: Bauteil1.5V, DHT11.Vcc, Sparkfun_HX711.Pin_9, Sparkfun_HX711.Pin_10, M2.pin3, M3.pin3, J1.vcc, WL-134.VCC
  GND: Bauteil1.GND, DHT11.GND, Sparkfun_HX711.Pin_6, M2.pin2, M3.pin2, J1.gnd, WL-134.GND
  N3: Bauteil1.D30, DHT11.Data
  N4: Bauteil1.D34, Sparkfun_HX711.Pin_7
  N5: Bauteil1.D36, Sparkfun_HX711.Pin_8
  N6: Bauteil1.D40, M2.pin1
  N7: Bauteil1.D43, WL-134.MISO
  N8: Bauteil1.D45, WL-134.RST
  N9: Bauteil1.D46, J1.pulse
  N10: Adafruit_DS3231_RTC.GND, A1.Pin_22, A1.Pin_29
  N11: Adafruit_DS3231_RTC.VCC, A1.Pin_27, A1.Pin_28
  N12: Adafruit_DS3231_RTC.SDA, A1.Pin_125
  N13: Adafruit_DS3231_RTC.SCL, A1.Pin_124

custom parts:
  Humidity and Temperature Sensor DHT11: Digital relative humidity & temperature sensor DHT11
  Sparkfun load cell amplifier: The SparkFun Load Cell Amplifier is a small breakout board for the HX711 IC that allows you to easily read load cells to measure weight.
  Arduino GIGA R1 WiFi: The Arduino GIGA R1 WiFi is designed for ambitious makers who want to step up their game.
  RFID RC522 SIP - 8 pins: A SIP stand-in part for RFID RC522 . With 8 pins on a 300 mil single inline package (SIP) footprint.
